# Fritzing sketch LSA_200617.1_fritzing (saved by Fritzing 0.9.3b)
breadboards: 1

parts:
  LED1 = LED - 5mm [color="Red (633nm)" package="5 mm [THT]"]
  LED2 = LED - 5mm [color="Yellow (595nm)" package="5 mm [THT]"]
  LED3 = LED - 5mm [color="Green (555nm)" package="5 mm [THT]"]
  LED4 = LED - 5mm [color="Red (633nm)" package="5 mm [THT]"]
  LED5 = LED - 5mm [color="Yellow (595nm)" package="5 mm [THT]"]
  LED6 = LED - 5mm [color="Green (555nm)" package="5 mm [THT]"]
  R1 = Resistor [tolerance=±5% resistance=1k package=THT]
  R2 = Resistor [tolerance=±5% resistance=1k package=THT]
  R3 = Resistor [tolerance=±5% resistance=1k package=THT]
  R4 = Resistor [tolerance=±5% resistance=1k package=THT]
  R5 = Resistor [tolerance=±5% resistance=1k package=THT]
  R6 = Resistor [tolerance=±5% resistance=1k package=THT]
  Taster_Nebenstraße = Pushbutton [package=THT]
  R7 = Resistor [tolerance=±5% resistance=1k package=THT]
  Taster_Abbieger = Pushbutton [package=THT]
  R8 = Resistor [tolerance=±5% resistance=1k package=THT]
  Taster_Straßenbahn = Pushbutton [package=THT]
  R9 = Resistor [tolerance=±5% resistance=1k package=THT]
  Bauteil1 = Arduino Mega 2560 (Rev3)
  LED7 = LED - 5mm [color="Red (633nm)" package="5 mm [THT]"]
  LED8 = LED - 5mm [color="Yellow (595nm)" package="5 mm [THT]"]
  LED9 = LED - 5mm [color="Green (555nm)" package="5 mm [THT]"]
  R10 = Resistor [tolerance=±5% resistance=1k package=THT]
  R11 = Resistor [tolerance=±5% resistance=1k package=THT]
  R12 = Resistor [tolerance=±5% resistance=1k package=THT]
  LED10 = LED - 5mm [color="Blue (430nm)" package="5 mm [THT]"]
  LED11 = LED - 5mm [color="White (4500K)" package="5 mm [THT]"]
  R13 = Resistor [tolerance=±5% resistance=1k package=THT]
  R14 = Resistor [tolerance=±5% resistance=1k package=THT]
  Taster_Zeitschaltung = Pushbutton [package=THT]
  Taster_Sensorschaltung = Pushbutton [package=THT]
  R15 = Resistor [tolerance=±5% resistance=1k package=THT]
  R16 = Resistor [tolerance=±5% resistance=1k package=THT]

nets:
  N1: LED1.cathode, LED2.cathode, LED3.cathode, LED4.cathode, LED5.cathode, LED6.cathode, Taster_Nebenstraße.leg0, Taster_Abbieger.leg0, Taster_Straßenbahn.leg0, Bauteil1.GND, LED7.cathode, LED8.cathode, LED9.cathode, LED10.cathode, LED11.cathode, Taster_Zeitschaltung.leg0, Taster_Sensorschaltung.leg0
  N2: LED1.anode, R1.Pin_1
  N3: LED2.anode, R2.Pin_1
  N4: LED3.anode, R3.Pin_1
  N5: LED4.anode, R5.Pin_1
  N6: LED5.anode, R4.Pin_1
  N7: LED6.anode, R6.Pin_1
  N8: R1.Pin_0, Bauteil1.D11_PWM
  N9: R2.Pin_0, Bauteil1.D12_PWM
  N10: R3.Pin_0, Bauteil1.D13_PWM
  N11: R4.Pin_0, Bauteil1.D3_PWM
  N12: R5.Pin_0, Bauteil1.D2_PWM
  N13: R6.Pin_0, Bauteil1.D4_PWM
  N14: Taster_Nebenstraße.leg1, R7.Pin_1, Bauteil1.D20/SDA
  N15: R7.Pin_0, R8.Pin_0, R9.Pin_0, Bauteil1.5V, R15.Pin_1, R16.Pin_1
  N16: Taster_Abbieger.leg1, R8.Pin_1, Bauteil1.D21/SCL
  N17: Taster_Straßenbahn.leg1, R9.Pin_1, Bauteil1.D22
  N18: Bauteil1.D15/RX3, R14.Pin_0
  N19: Bauteil1.D14/TX3, R13.Pin_0
  N20: Bauteil1.D5_PWM, R12.Pin_0
  N21: Bauteil1.D6_PWM, R11.Pin_0
  N22: Bauteil1.D7_PWM, R10.Pin_0
  N23: Bauteil1.D25, Taster_Zeitschaltung.leg1, R15.Pin_0
  N24: Bauteil1.D26, Taster_Sensorschaltung.leg1, R16.Pin_0
  N25: LED7.anode, R12.Pin_1
  N26: LED8.anode, R11.Pin_1
  N27: LED9.anode, R10.Pin_1
  N28: LED10.anode, R14.Pin_1
  N29: LED11.anode, R13.Pin_1

notes:
  Abbieger Hauptstraße
  Straßenbahn,
  Blau =Rot, Weiß=Grün
  Hauptstraße
  Nebenstraße
